# Fritzing sketch circuit (saved by Fritzing 0.7.11b)
stripboards: 1

parts:
  J1 = female pin header, 4 pins [form="♀ (female)"]
  IC1 = H-Bridge [package=THT]
  U1 = atmega168 [package="DIP28 [THT]"]
  LED1 = LED - 5mm [color="Red (633nm)" package="5 mm [THT]"]
  Q1 = NPN-Transistor [package="TO92 [THT]"]
  J3 = shrouded pin header, 6 pins [form="♂ (shrouded male)"]
  C1 = Ceramic Capacitor [capacitance=10pF package="100 mil [THT, multilayer]"]
  XTAL1 = CRYSTAL - kHz [frequency="16 Mhz"]
  C2 = Ceramic Capacitor [capacitance=10pF package="100 mil [THT, multilayer]"]
  R1 = Resistor [tolerance=±5% resistance=15k package=THT]

nets:
  N1: J1.pin1, IC1.4Y
  N2: J1.pin2, IC1.2Y
  N3: J1.pin3, IC1.1Y
  N4: J1.pin4, IC1.3Y
  GND1: IC1.1_2EN, IC1.GND1, IC1.GND2, IC1.VCC2, IC1.3_4EN, IC1.GND3, IC1.GND4, IC1.VCC1, U1.Pin_7, U1.Pin_8, U1.Pin_9, U1.Pin_20, U1.Pin_21, U1.Pin_22, LED1.cathode, Q1.C, J3.pin4, J3.pin6, C1.0, C1.1, XTAL1.pin_0, C2.1, R1.Pin_0
  N5: IC1.1A, U1.Pin_14, U1.Pin_15, Q1.B
  N6: IC1.2A, IC1.3A, U1.Pin_12, U1.Pin_17, J3.pin5
  N7: IC1.4A, U1.Pin_13, U1.Pin_16
  N8: U1.Pin_1, J3.pin3, R1.Pin_1
  N9: U1.Pin_4, U1.Pin_25
  N10: U1.Pin_5, U1.Pin_24
  N11: U1.Pin_6, U1.Pin_23
  N12: U1.Pin_10, U1.Pin_19, J3.pin2, XTAL1.pin_1, C2.0
  N13: U1.Pin_11, U1.Pin_18, J3.pin1
  N14: LED1.anode, Q1.E
